# Fritzing sketch tracker (saved by Fritzing 0.9.3b)
breadboards: 1

parts:
  Controller = Arduino Uno (Rev3)
  Pulse_Sensor = mystery part, 3 pins [chip_label="Pulse Sensor (3-5 V)"]
  Bluetooth = mystery part, 4 pins [chip_label="Bluetooth HC-06"]

nets:
  N1: Controller.A0, Pulse_Sensor.pin3
  N2: Controller.GND, Pulse_Sensor.pin2
  N3: Controller.D0/RX, Bluetooth.pin1
  N4: Controller.D1/TX, Bluetooth.pin2
  N5: Controller.3V3, Pulse_Sensor.pin1, Bluetooth.pin3
  GND: Bluetooth.pin4
